# Fritzing sketch traffic controll system (saved by Fritzing 0.9.3b)
breadboards: 1

parts:
  Part1 = Arduino Uno (Rev3)
  hc-sr1 = hc-sr04
  hc-sr2 = hc-sr04
  hc-sr3 = hc-sr04
  hc-sr4 = hc-sr04
  J1 = Basic Servo
  J3 = Basic Servo
  J4 = Basic Servo
  J5 = Basic Servo

nets:
  N1: Part1.D8, J1.pulse
  N2: Part1.D9_PWM, hc-sr4.Trig
  N3: Part1.D10_PWM/SS, hc-sr3.Echo
  N4: Part1.D11_PWM/MOSI, hc-sr3.Trig
  N5: Part1.D12/MISO, J3.pulse
  N6: Part1.D13/SCK, J4.pulse
  N7: Part1.D2, hc-sr1.Echo
  N8: Part1.D3_PWM, hc-sr1.Trig
  N9: Part1.D4, J5.pulse
  N10: Part1.D5_PWM, hc-sr4.Echo
  N11: Part1.D6_PWM, hc-sr2.Echo
  N12: Part1.D7, hc-sr2.Trig
  GND: Part1.GND, hc-sr1.GND, hc-sr2.GND, hc-sr3.GND, hc-sr4.GND, J1.gnd, J3.gnd, J4.gnd, J5.gnd
  VCC: Part1.VIN, hc-sr1.VCC, hc-sr2.VCC, hc-sr3.VCC, hc-sr4.VCC, J1.vcc, J3.vcc, J4.vcc, J5.vcc
